# Fritzing sketch arduino_L298N_2motors (saved by Fritzing 0.9.3b)

parts:
  Part1 = Arduino Mega 2560 (Rev3)
  S1 = H-Bridge with L298N
  Power_plug1 = Power plug
  M1 = DC Motor
  M2 = DC Motor

nets:
  N1: Part1.D9_PWM, S1.ENA
  N2: Part1.D8_PWM, S1.IN1
  5V: Part1.5V, S1.5V
  GND: Part1.GND, S1.GND, Power_plug1.GND
  N3: Part1.D3_PWM, S1.ENB
  N4: Part1.D4_PWM, S1.IN4
  N5: Part1.D5_PWM, S1.IN3
  N6: Part1.D7_PWM, S1.IN2
  12V: S1.12V, Power_plug1.VCC
  N7: S1.M1-01, M2.pin_2
  N8: S1.M1-02, M2.pin_1
  N9: S1.M2-01, M1.pin_2
  N10: S1.M2-02, M1.pin_1

notes:
  ENABLE pins need to be connected to Arduino pins supporting PWM
  Arduino UNO: 3,5,6,9,10,11
  Arduino MEGA: 2-13, 44-46
  Remove all jumpers from the L298N

custom parts:
  H-Bridge with L298N: h-bridge
