# Fritzing sketch arduino_LED (saved by Fritzing 0.9.3b)

parts:
  Part1 = Arduino Uno (Rev3)
  LED1 = smd LED [color="Red (633nm)" package="0603 [SMD]"]
  R1 = Resistor [tolerance=±5% resistance=220 package="0402 [SMD]"]

nets:
  N1: Part1.D9_PWM, R1.Pin_1
  N2: Part1.GND, LED1.cathode
