# Fritzing sketch arduino_electromagnet (saved by Fritzing 0.9.3b)

parts:
  L1 = Solenoid
  KY-1 = Relay [package=THT]
  Power_plug1 = Power plug
  Part1 = Arduino Mega 2560 (Rev3)

nets:
  N1: L1.pin1, Power_plug1.GND
  N2: L1.pin2, KY-1.NO
  N3: KY-1.power, Part1.5V
  N4: KY-1.ground, Part1.GND
  N5: KY-1.in, Part1.D8_PWM

notes:
  power supply for electromagnet (check voltage requirement needed for electromagnet)
  electromagnet /
  push-pull solenoid /
  lock-style solenoid

custom parts:
  Relay: The Keyes 5V relay module is suitable for SCM development, home appliance control. It uses a 5V~12V TIL control signal which can control DC / AC signal.
