# Fritzing sketch arduino_electromagnet_transistor (saved by Fritzing 0.9.3b)
breadboards: 1

parts:
  L1 = Solenoid
  Power_plug1 = Power plug
  Part1 = Arduino Uno (Rev3)
  Q1 = NPN-Transistor [package="TO92 [THT]"]
  D1 = Diode [package=diode-1n4001]

nets:
  N1: L1.pin1, Q1.C, D1.A
  N2: L1.pin2, Power_plug1.VCC, D1.C
  GND: Power_plug1.GND, Part1.GND, Q1.E
  N3: Part1.D3_PWM, Q1.B

notes:
  power supply for electromagnet (check voltage requirement needed for electromagnet)
  in my case, it is 12V
  electromagnet /
  push-pull solenoid /
  lock-style solenoid
  PN2222 transistor
  (EBC pinout)
  1N4001 diode
