# Fritzing sketch arduino_fan_onoff (saved by Fritzing 0.9.3b)

parts:
  KY-1 = Relay [package=THT]
  Power_plug1 = Power plug
  Part1 = Arduino Mega 2560 (Rev3)
  F1 = Fan - Ventilador [package=THT]

nets:
  N1: KY-1.power, Part1.5V
  N2: KY-1.ground, Part1.GND
  N3: KY-1.in, Part1.D8_PWM
  N4: KY-1.NO, F1.5V
  GND: Power_plug1.GND, F1.GND

notes:
  power supply for fan (check voltage requirement needed for fan)
  Simple setup to just turn on and off (no speed control)

custom parts:
  Relay: The Keyes 5V relay module is suitable for SCM development, home appliance control. It uses a 5V~12V TIL control signal which can control DC / AC signal.
  Fan - Ventilador: Ventilador de 2 pines, se encuentra comunmente en computadoras de escritorio
