# Fritzing sketch arduino_suction_cup (saved by Fritzing 0.9.3b)

parts:
  Power_plug1 = Power plug
  KY-1 = Keyes Relay [package=THT]
  KY-2 = Keyes Relay [package=THT]
  Part1 = Arduino Mega 2560 (Rev3)
  M1 = DC Motor
  L1 = Solenoid

nets:
  N1: Power_plug1.GND, L1.pin2
  N2: Power_plug1.VCC, KY-2.C
  N3: KY-1.signal, Part1.D8_PWM
  N4: KY-1.power, Part1.5V
  N5: KY-1.ground, Part1.GND
  N6: KY-1.NO, M1.pin_1
  N7: KY-2.signal, Part1.D7_PWM
  N8: KY-2.NO, L1.pin1

notes:
  Air pump
  Solenoid Valve
  ^
  |
  AIR OUT
  <--- AIR IN
  External power supply
  (check voltage requirements of the air pump motor)
  Suction cup
  ^
  |
  Release air OUT (when solenoid activated)
  General operation of a pick and place scenario
  (note: movement operations not included in the diagram)
  * Move suction cup on top of the object to be picked up
  * Turn on pump, leave solenoid valve at rest (means there is a direct connection between pump and suction cup)
  * Move to pick up object
  * Turn on solenoid valve (the connection on the vent is blocked, and object can fall), turn off the pump

custom parts:
  Keyes Relay: The Keyes 5V relay module is suitable for SCM development, home appliance control. It uses a 5V~12V TIL control signal which can control DC / AC signal.
