# Fritzing sketch arduino_suction_transistor (saved by Fritzing 0.9.3b)
breadboards: 1

parts:
  Power_plug1 = Power plug
  M1 = DC Motor
  L1 = Solenoid
  Part1 = Arduino Uno (Rev3)
  Q2 = NPN-Transistor [package="TO92 [THT]"]
  D2 = Diode [package=diode-1n4001]
  Q3 = NPN-Transistor [package="TO92 [THT]"]
  D3 = Diode [package=diode-1n4001]

nets:
  GND: Power_plug1.GND, Part1.GND, Q2.E, Q3.E
  N1: Power_plug1.VCC, M1.pin_2, L1.pin2, D2.C, D3.C
  N2: M1.pin_1, Q2.C, D2.A
  N3: L1.pin1, Q3.C, D3.A
  N4: Part1.D3_PWM, Q2.B
  N5: Part1.D5_PWM, Q3.B

notes:
  Air pump
  Solenoid Valve
  ^
  |
  AIR OUT
  <--- AIR IN
  External power supply
  (check voltage requirements of the air pump motor)
  In my case, 12V
  Suction cup
  ^
  |
  Release air OUT (when solenoid activated)
  General operation of a pick and place scenario
  (note: movement operations not included in the diagram)
  * Move suction cup on top of the object to be picked up
  * Turn on pump, leave solenoid valve at rest (means there is a direct connection between pump and suction cup)
  * Move to pick up object
  * Turn on solenoid valve (the connection on the vent is blocked, and object can fall), turn off the pump
  PN2222 transistor
  (EBC pinout)
  1N4001 diode
